# Fritzing sketch glove controller (saved by Fritzing 0.9.9b)
breadboards: 1

parts:
  U1 = Arduino Uno (Rev3)
  IMU = InvenSense MPU6050
  Bluetooth_module = Bluetooth HC-05 Macho
  F1 = Basic Flex Resistor
  R1 = Resistor [tolerance=±5% resistance=10k package="2010 [SMD]"]
  F2 = Basic Flex Resistor
  R2 = Resistor [tolerance=±5% resistance=10k package="2010 [SMD]"]
  F3 = Basic Flex Resistor
  R3 = Resistor [tolerance=±5% resistance=10k package="2010 [SMD]"]
  F4 = Basic Flex Resistor
  R4 = Resistor [tolerance=±5% resistance=10k package="2010 [SMD]"]
  S1 = Pushbutton [package=THT]
  VCC1 = Battery block 9V

nets (from the breadboard view):
  N1: U1.A0, F1.pin_1, R1.Pin_1
  N2: U1.A1, F2.pin_1, R2.Pin_1
  N3: U1.A2, F3.pin_1, R3.Pin_1
  N4: U1.A3, F4.pin_1, R4.Pin_1
  N5: U1.A4/SDA, IMU.SDA
  N6: U1.A5/SCL, IMU.SCL
  N7: U1.D0/RX, Bluetooth_module.RXD
  N8: U1.D1/TX, Bluetooth_module.TXD
  VCC: U1.5V, IMU.VCC, Bluetooth_module.VCC, R1.Pin_0, R2.Pin_0, R3.Pin_0, R4.Pin_0
  GND: U1.GND, IMU.GND, Bluetooth_module.GND, F1.Pin_2, F2.Pin_2, F3.Pin_2, F4.Pin_2, S1.leg0
  N9: U1.VIN, VCC1.+
  N10: S1.leg1, VCC1.-
