# Fritzing sketch glove_v2 (saved by Fritzing 0.9.9b)
breadboards: 1

parts:
  Microcontroller = Arduino Uno (Rev3)
  IMU = InvenSense MPU6050
  F1 = Basic Flex Resistor
  R1 = Resistor [tolerance=±5% resistance=10k package="2010 [SMD]"]
  F2 = Basic Flex Resistor
  R2 = Resistor [tolerance=±5% resistance=10k package="2010 [SMD]"]
  F3 = Basic Flex Resistor
  R3 = Resistor [tolerance=±5% resistance=10k package="2010 [SMD]"]
  F4 = Basic Flex Resistor
  R4 = Resistor [tolerance=±5% resistance=10k package="2010 [SMD]"]
  S1 = Pushbutton [package=THT]
  VCC1 = Battery block 9V
  Transmitter = NRF24L01+ Breakout Board
  U3 = Voltage Regulator - 3.3V [package="TO220 [THT]"]
  C1 = Capacitor Polarized [package=panasonic_c]

nets (from the breadboard view):
  N1: Microcontroller.A0, F1.pin_1, R1.Pin_1
  N2: Microcontroller.A1, F2.pin_1, R2.Pin_1
  N3: Microcontroller.A2, F3.pin_1, R3.Pin_1
  N4: Microcontroller.A3, F4.pin_1, R4.Pin_1
  N5: Microcontroller.A4/SDA, IMU.SDA
  N6: Microcontroller.A5/SCL, IMU.SCL
  N7: Microcontroller.D9_PWM, Transmitter.CE
  N8: Microcontroller.D10_PWM/SS, Transmitter.CS
  N9: Microcontroller.D11_PWM/MOSI, Transmitter.MOSI
  N10: Microcontroller.D12/MISO, Transmitter.MISO
  N11: Microcontroller.D13/SCK, Transmitter.SCK
  GND: Microcontroller.GND, IMU.GND, F1.Pin_2, F2.Pin_2, F3.Pin_2, F4.Pin_2, S1.leg0, Transmitter.GND, U3.GND, C1.-
  5V: Microcontroller.5V, IMU.VCC, R1.Pin_0, R2.Pin_0, R3.Pin_0, R4.Pin_0
  N12: Microcontroller.VIN, VCC1.+, U3.input_voltage
  N13: S1.leg1, VCC1.-
  N14: Transmitter.VCC, U3.output_voltage, C1.+
