# Fritzing sketch glove_v3 (saved by Fritzing 0.9.9b)
breadboards: 2

parts:
  Part1 = Arduino Uno (Rev3)
  Part2 = NRF24L01+ Breakout Board
  U1 = LIPO-2000mAh [package=lipo-2000]
  C1 = Capacitor Polarized [package=panasonic_c]
  U4 = Voltage Regulator - 3.3V [package="TO220 [THT]"]
  S2 = Pushbutton [package=THT]
  R2 = Resistor [tolerance=±5% resistance=10k package="2010 [SMD]"]
  R3 = Resistor [tolerance=±5% resistance=10k package="2010 [SMD]"]
  R4 = Resistor [tolerance=±5% resistance=10k package="2010 [SMD]"]
  IMU1 = InvenSense MPU6050
  F5 = Basic Flex Resistor
  F6 = Basic Flex Resistor
  F7 = Basic Flex Resistor

nets:
  N1: Part1.A0, R4.Pin_1, F6.pin_1
  N2: Part1.A1, R3.Pin_1, F7.pin_1
  N3: Part1.A2, R2.Pin_1, F5.pin_1
  N4: Part1.A4/SDA, IMU1.SDA
  N5: Part1.A5/SCL, IMU1.SCL
  N6: Part1.D9_PWM, Part2.CE
  N7: Part1.D10_PWM/SS, Part2.CS
  N8: Part1.D11_PWM/MOSI, Part2.MOSI
  N9: Part1.D12/MISO, Part2.MISO
  N10: Part1.D13/SCK, Part2.SCK
  GND: Part1.GND, Part2.GND, U1.-, C1.-, U4.GND, IMU1.GND, F5.Pin_2, F6.Pin_2, F7.Pin_2
  5V: Part1.5V, R2.Pin_0, R3.Pin_0, R4.Pin_0, IMU1.VCC
  N11: Part1.VIN, U1.+, U4.input_voltage, S2.leg0, S2.leg1
  N12: Part2.VCC, C1.+, U4.output_voltage
